// Logisim project alu.circ as structural Verilog: 1 circuit, main circuit alu
module alu (
  input  [31:0] A,
  input  [31:0] B,
  input  [3:0] ALUSel,
  output [31:0] ALUResult
);

  wire LTbit;
  wire [31:0] a0, a1, a2, a3, a4, a5, a6, a7, add0, b0, b1, b2, b3, c0, c1, mh_lo, mhu_lo, r0000, r0001,
       r0100, r0101, r0110, r0111, r1000, r1100, r1101;
  wire [63:32] As64, Bs64, mh_p, mhu_p;

  Adder #(.width(32)) adder_1 (.a(A), .b(B), .out(add0));  // open: cin, cout
  Adder #(.width(32)) adder_2 (.a(A), .b(B), .out(r0000));  // open: cin, cout
  Subtractor #(.width(32)) subtractor_1 (.a(A), .b(B), .out(r1100));  // open: bin, bout
  assign r0100 = A ^ B;  // XOR_Gate xor_1, 32 bits wide
  assign r0110 = A | B;  // OR_Gate or_1, 32 bits wide
  assign r0111 = A & B;  // AND_Gate and_1, 32 bits wide
  Multiplier #(.width(32)) multiplier_1 (.a(A), .b(B), .out(r1000));  // open: cin, cout
  Shifter #(.width(32), .shift("ll")) shifter_1 (.in(A), .\dist (B[4:0]), .out(r0001));
  Shifter #(.width(32), .shift("lr")) shifter_2 (.in(A), .\dist (B[4:0]), .out(r0101));
  Shifter #(.width(32), .shift("ar")) shifter_3 (.in(A), .\dist (B[4:0]), .out(r1101));
  Comparator #(.width(32), .mode("twosComplement")) comparator_1 (.a(A), .b(B), .lt(LTbit));  // open: gt, eq
  Multiplier #(.width(64)) multiplier_2 (
    .a({{32{1'b0}}, A}), .b({{32{1'b0}}, B}), .out({mhu_p, mhu_lo}));  // open: cin, cout
  Multiplexer #(.width(32), .select(1)) multiplexer_1 (.in0({32{1'b0}}), .in1({32{1'b1}}), .out(As64), .sel(A[31]));
  Multiplexer #(.width(32), .select(1)) multiplexer_2 (.in0({32{1'b0}}), .in1({32{1'b1}}), .out(Bs64), .sel(B[31]));
  Multiplier #(.width(64)) multiplier_3 (.a({As64, A}), .b({Bs64, B}), .out({mh_p, mh_lo}));  // open: cin, cout
  Multiplexer #(.width(32), .select(1)) multiplexer_3 (.in0(r0000), .in1(r0001), .out(a0), .sel(ALUSel[0]));
  Multiplexer #(.width(32), .select(1)) multiplexer_4 (
    .in0({{31{1'b0}}, LTbit}), .in1({32{1'b0}}), .out(a1), .sel(ALUSel[0]));
  Multiplexer #(.width(32), .select(1)) multiplexer_5 (.in0(r0100), .in1(r0101), .out(a2), .sel(ALUSel[0]));
  Multiplexer #(.width(32), .select(1)) multiplexer_6 (.in0(r0110), .in1(r0111), .out(a3), .sel(ALUSel[0]));
  Multiplexer #(.width(32), .select(1)) multiplexer_7 (.in0(r1000), .in1(mh_p), .out(a4), .sel(ALUSel[0]));
  Multiplexer #(.width(32), .select(1)) multiplexer_8 (.in0({32{1'b0}}), .in1(mhu_p), .out(a5), .sel(ALUSel[0]));
  Multiplexer #(.width(32), .select(1)) multiplexer_9 (.in0(r1100), .in1(r1101), .out(a6), .sel(ALUSel[0]));
  Multiplexer #(.width(32), .select(1)) multiplexer_10 (.in0({32{1'b0}}), .in1(B), .out(a7), .sel(ALUSel[0]));
  Multiplexer #(.width(32), .select(1)) multiplexer_11 (.in0(a0), .in1(a1), .out(b0), .sel(ALUSel[1]));
  Multiplexer #(.width(32), .select(1)) multiplexer_12 (.in0(a2), .in1(a3), .out(b1), .sel(ALUSel[1]));
  Multiplexer #(.width(32), .select(1)) multiplexer_13 (.in0(a4), .in1(a5), .out(b2), .sel(ALUSel[1]));
  Multiplexer #(.width(32), .select(1)) multiplexer_14 (.in0(a6), .in1(a7), .out(b3), .sel(ALUSel[1]));
  Multiplexer #(.width(32), .select(1)) multiplexer_15 (.in0(b0), .in1(b1), .out(c0), .sel(ALUSel[2]));
  Multiplexer #(.width(32), .select(1)) multiplexer_16 (.in0(b2), .in1(b3), .out(c1), .sel(ALUSel[2]));
  Multiplexer #(.width(32), .select(1)) multiplexer_17 (.in0(c0), .in1(c1), .out(ALUResult), .sel(ALUSel[3]));

  // Other names for the same wires on the sheet: S0 = ALUSel[0]; S1 = ALUSel[1]; S2 = ALUSel[2]; S3 = ALUSel[3];
  //   A_lo31[30:0] = A[30:0]; As64[31:0] = A; Au64[31:0] = A; A_b31 = A[31]; Asgn[31:0] = As64;
  //   B_lo31[30:0] = B[30:0]; Bs64[31:0] = B; Bsh5[4:0] = B[4:0]; Bu64[31:0] = B; r1111[31:0] = B;
  //   Bhi27[26:0] = B[31:5]; B_b31 = B[31]; Bsgn[31:0] = Bs64; mh_p[31:0] = mh_lo; r1001[31:0] = mh_p;
  //   mhu_p[31:0] = mhu_lo; r1011[31:0] = mhu_p; r0010[0] = LTbit

  // Notes on the sheet:
  //   INPUTS to your circuit
  //   DON'T CHANGE THE LOCATIONS OF THE INPUTS AND OUTPUTS!
  //   OUTPUT from your circuit
endmodule
